# Fritzing sketch Arduino Circuit (saved by Fritzing 0.9.3b)

parts:
  U1 = NodeMCU V3.0
  DHT11_1 = DHT11 module
  Relay = KY-019 5V Relay Module [package="Breakout board"]
  J1 = Screw terminal - 2 pins [package=THT]
  R1 = Resistor [tolerance=±5% resistance=39k package="0805 [SMD]"]

nets:
  N1: U1.D4, DHT11_1.DATA
  3V3: U1.3V3, DHT11_1.VCC, Relay.+, J1.pin2
  GND: U1.GND, DHT11_1.GND, Relay.-, R1.Pin_1
  N2: U1.D6, Relay.S
  N3: U1.D7, J1.pin1, R1.Pin_0

custom parts:
  NodeMCU V3.0: ESP8266 based NodeMCU
  DHT11 module: DHT11 black pcb module
  KY-019 5V Relay Module: KY-019 5V Relay module, used to control AC circuits. (Special thanks to vanepp for fixing the PCB holes and other errors)
